# Fritzing sketch MicroWaveTimer (saved by Fritzing 0.9.3b)
circuit board: 7.11874cm x 5.78896cm
breadboards: 2

parts:
  PIC16F1690 = PIC16F690 [part_number=PIC16F690 package="DIP (Dual Inline) [THT]"]
  FTDI_TTL_232R-5V_USB = PIC ICSP - 5 pins [form="♂ (male)" package=THT]
  LCD1 = LCD screen  # not connected
  Pin_6-10 = PIC ICSP - 5 pins [form="♂ (male)" package=THT]
  Pin_11-15 = PIC ICSP - 5 pins [form="♂ (male)" package=THT]
  Resistor_1kΩ = Resistor [tolerance=±0.05% resistance=1k package=THT]
  Resistor_1kΩ_2 = Resistor [tolerance=±5% resistance=21k package="2512 [SMD]"]
  Potentometer_for_Screen = POT [package=3362u]
  Pin_1-5 = male pin header, 5 pins [form="♂ (male)"]
  Potentiometer_for_Picking_Minute = Rotary Potentiometer (Small) [maximum_resistance=100kΩ package=THT]
  Button = Pushbutton [package="[THT]"]

nets (from the pcb view):
  N1: PIC16F1690.VDD, FTDI_TTL_232R-5V_USB.pin4, Resistor_1kΩ.Pin_0, Resistor_1kΩ_2.Pin_1, Potentometer_for_Screen.E, Pin_1-5.pin4, Potentiometer_for_Picking_Minute.leg1, Button.Pin_1, Button.Pin_2
  N2: PIC16F1690.RA3, FTDI_TTL_232R-5V_USB.pin5, Resistor_1kΩ.Pin_1
  N3: PIC16F1690.RC3, Pin_11-15.pin2
  N4: PIC16F1690.RB7, Resistor_1kΩ_2.Pin_0, Button.Pin_3, Button.Pin_4
  N5: PIC16F1690.RB6, Pin_6-10.pin5
  N6: PIC16F1690.RB4, Pin_1-5.pin2
  N7: PIC16F1690.RC2, Pin_11-15.pin3
  N8: PIC16F1690.RC1, Pin_11-15.pin4
  N9: PIC16F1690.RC0, Pin_11-15.pin5
  N10: PIC16F1690.RA2, Potentiometer_for_Picking_Minute.wiper
  N11: PIC16F1690.RA1, FTDI_TTL_232R-5V_USB.pin1
  N12: PIC16F1690.RA0, FTDI_TTL_232R-5V_USB.pin2
  N13: PIC16F1690.VSS, FTDI_TTL_232R-5V_USB.pin3, Potentometer_for_Screen.A, Pin_1-5.pin1, Pin_1-5.pin5, Potentiometer_for_Picking_Minute.leg2
  N14: Potentometer_for_Screen.S, Pin_1-5.pin3

notes:
  FTDI TTL_232R-5V USB
  for serial monitor
  (optional)
  FTDI TTL-232R-5V
  (optional)
  PICkit 2 ICSP programmer ICP01
  +5V
  GND
  Microwave Timer
  You forgot that two of them are going to ground
  Follow the color to know where it is connected
  Poteintiomenter
  Varies from 0-1kOhms
  Potentiometer
  Varies from 0-1kOhms
  LCD screen 2x16
  https://www.electrokit.com/lcd-2x16-tecken-tn-led.43249?gclid=CjwKEAjwl9DIBRCG_e3DwsKsizsSJADMmJ113dSmrxSExkpXn3KxNVe9hCMj1nLnfekC5uw7kBWFAhoC9hLw_wcB
  pizza
  note here]

custom parts:
  PIC16F690: PIC® Flash microcontroller mid-range x14 architecture 2.0-5.5 volts, internal oscillator 8 MHz - 32 KHz, EEPROM, nanoWatt Technology. 12 channels of 10-bit A/D, two comparators, on-chip voltage reference, Enhanced Capture/Compare/PWM, EUSART, SPI/I2C.
  PIC ICSP - 5 pins: PIC ICSP programmer connection (ICP01 PICkit 2 sw)

// code stored in the sketch: blinka.c
/* blinka.c  PICkit 2 LPC DS1 or breadboard  */ 
/* B Knudsen Cc5x C-compiler - not ANSI-C */
#include "16F690.h"
#pragma config |= 0x00D4 
void delay10( char );
 
void main( void)
{
  TRISC.0 = 0;  /* PORTC pin 0 output */
  
  while(1)
    {
       delay10(10);
	   PORTC.0 = 1; /* PORTC pin 0 "1" */
	   delay10(10);
	   PORTC.0 = 0; /* PORTC pin 0 "0" */
    }
}


/* *********************************** */
/*            FUNCTIONS                */
/* *********************************** */


void delay10( char n)
/*
  Delays a multiple of 10 milliseconds using the TMR0 timer
  Clock : 4 MHz   => period T = 0.25 microseconds
  1 IS = 1 Instruction Cycle = 1 microsecond
  error: 0.16 percent
*/
{
    char i;

    OPTION = 7;
    do  {
        i = TMR0 + 39; /* 256 microsec * 39 = 10 ms */
        while ( i != TMR0)
            ;
    } while ( --n > 0);
}


/* *********************************** */
/*            HARDWARE                 */
/* *********************************** */

/*
             _____________  _____________ 
            |             \/             |
      +5V---|Vdd        16F690        Vss|---Gnd
            |RA5            RA0/AN0/(PGD)|
            |RA4/AN3            RA1/(PGC)|
            |RA3/!MCLR/(Vpp)  RA2/AN2/INT|
            |RC5/CCP                  RC0|->-LED0
            |RC4                      RC1|
            |RC3/AN7                  RC2|
            |RC6/AN8             AN10/RB4|
            |RC7/AN9               RB5/Rx|
            |RB7/Tx                   RB6|
            |____________________________|
                                          
*/

// code stored in the sketch: hejsan.c
/* hello_blink.c  PICkit 2 breadboard LED + bitbanging com */ 
/* hello_blink.c  PICkit 2 breadboard LED + bitbanging com */ 
/* Blink with LED, receive char and printout loop count    */

/* B Knudsen Cc5x C-compiler - not ANSI-C */
#include <16F690.h>
#include <int16Cxx.h>
#pragma config |= 0x00D4 

/* FUNCTION PROTOTYPES */
void delay10( char );
void init_serial( void );
void putchar( char);
void printf(const char *string, char variable);

/* GLOBAL VARIABLES */
bit receiver_flag;   /* Signal-flag used by interrupt routine   */
char receiver_byte;  /* Transfer Byte used by interrupt routine */

/* INTERRUPT ROUTINE */
/* Interrupt routine - receiving chars at need */ 
#pragma origin 4
interrupt int_server( void ) /* the place for the interrupt routine */
{
  int_save_registers
  /* New interrupts are automaticaly disabled            */
  /* "Interrupt on change" at pin RA1 from PK2 UART-tool */
  
  if( PORTA.1 == 0 )  /* Interpret this as the startbit  */
    {  /* Receive one full character   */
      char bitCount, ti;
      /* delay 1,5 bit 156 usec at 4 MHz         */
      /* 5+28*5-1+1+2+9=156 without optimization */
      ti = 28; do ; while( --ti > 0); nop(); nop2();
      for( bitCount = 8; bitCount > 0 ; bitCount--)
       {
         Carry = PORTA.1;
         receiver_byte = rr( receiver_byte);  /* rotate carry */
         /* delay one bit 104 usec at 4 MHz       */
         /* 5+18*5-1+1+9=104 without optimization */ 
         ti = 18; do ; while( --ti > 0); nop(); 
        }
      receiver_flag = 1; /* A full character is now received */
    }
  RABIF = 0;    /* Reset the RABIF-flag before leaving   */
  int_restore_registers
  /* New interrupts are now enabled */
}


 /* MAIN PROGRAM */
void main( void)
{
    TRISC.0 = 0;   /* PORTC pin 0 output to LED     */
	TRISC.7 = 1;   /* PORTC pin 7 input from Button */
	ANSELH.1 = 0;  /* PORTC pin 7 not analog        */

    init_serial();
    char loopcounter=0;
	char speed = 100;
 
    receiver_flag=0;
  
    IOCA.1 = 1; /* PORTA.1 interrupt on change */
    RABIE =1;   /* interrupt on change         */
    GIE = 1;    /* interrupt enable            */
    
    delay10(100); /* wait one second */	
	printf("\r\nBlinks with LED\r\n",0); 
	printf("Receives char and then printout loop count.\r\n",0);
	printf("Fast blink if button is pressed.\r\n",0);
	
  while(1)
    {
	   if(!PORTC.7) speed=10; else speed=100; 
       delay10(speed);
	   PORTC.0 = 1; /* PORTC pin 0 "1" */
	   delay10(speed);
	   PORTC.0 = 0; /* PORTC pin 0 "0" */
	     if(receiver_flag) 
		   {
		     printf("\r\n", 0);
			 printf("%c ", receiver_byte);
		     printf("Loops = %u\r\n", loopcounter);
			 receiver_flag = 0;
		   }
	   loopcounter++;
    }
}




/* *********************************** */
/*            FUNCTIONS                */
/* *********************************** */

void delay10( char n)
/*
  Delays a multiple of 10 milliseconds using the TMR0 timer
  Clock : 4 MHz   => period T = 0.25 microseconds
  1 IS = 1 Instruction Cycle = 1 microsecond
  error: 0.16 percent
*/
{
    char i;

    OPTION = 7;
    do  {
        i = TMR0 + 39; /* 256 microsec * 39 = 10 ms */
        while ( i != TMR0)
            ;
    } while ( --n > 0);
}

void init_serial( void )  /* initialise PIC16F690 bitbang serialcom */
{
   ANSEL.0 = 0; /* No AD on RA0             */
   ANSEL.1 = 0; /* No AD on RA1             */
   PORTA.0 = 1; /* marking line             */
   TRISA.0 = 0; /* output to PK2 UART-tool  */
   TRISA.1 = 1; /* input from PK2 UART-tool */
   return;      
}

void putchar( char ch )  /* sends one char */
{
  char bitCount, ti;
  PORTA.0 = 0; /* set startbit */
  for ( bitCount = 10; bitCount > 0 ; bitCount-- )
   {
     /* delay one bit 104 usec at 4 MHz       */
     /* 5+18*5-1+1+9=104 without optimization */ 
     ti = 18; do ; while( --ti > 0); nop(); 
     Carry = 1;     /* stopbit                    */
     ch = rr( ch ); /* Rotate Right through Carry */
     PORTA.0 = Carry;
   }
  return;
}

void printf(const char *string, char variable) // printf look-alike
{
  char i, k, m, a, b;
  for(i = 0 ; ; i++)
   {
     k = string[i];
     if( k == '\0') break;   // at end of string
     if( k == '%')           // insert variable in string
      {
        i++;
        k = string[i];
        switch(k)
         {
           case 'd':         // %d  signed 8bit
             if( variable.7 ==1) putchar('-');
             else putchar(' ');
             if( variable > 127) variable = -variable;  // no break!
           case 'u':         // %u unsigned 8bit
             a = variable/100;
             putchar('0'+a); // print 100's
             b = variable%100;
             a = b/10;
             putchar('0'+a); // print 10's
             a = b%10;
             putchar('0'+a); // print 1's
             break;
           case 'x':         // %x HEX 8 bit
             static const char Hex_table[16] = "0123456789ABCDEF" ;
		     a = swap(variable);
             a = a & 0b0000.1111;
             b = Hex_table[a];
             putchar(b);
             a = variable & 0b0000.1111;
             b = Hex_table[a];
             putchar(b);
             break;
           case 'b':         // %b BINARY 8bit
             for( m = 0 ; m < 8 ; m++ )
              {
                if (variable.7 == 1) putchar('1');
                else putchar('0');
                variable = rl(variable);
               }
              break;
           case 'c':         // %c  'char'
             putchar(variable);
             break;
           case '%':
             putchar('%');
             break;
           default:          // not implemented
             putchar('!');
         }
      }
      else putchar(k);
   }
}





/* *********************************** */
/*            HARDWARE                 */
/* *********************************** */

/*
  Serial communication with PK2 UART-tool
  or used with TTL to USB Serial Converter
             _____________  _____________ 
            |             \/             |
      +5V---|Vdd        16F690        Vss|---Gnd
            |RA5            RA0/AN0/(PGD)|bbTx->- PK2 UART-tool
            |RA4/AN3            RA1/(PGC)|bbRx-<- PK2 UART-tool
            |RA3/!MCLR/(Vpp)  RA2/AN2/INT|
            |RC5/CCP                  RC0|->-LED0
            |RC4                      RC1|
            |RC3/AN7                  RC2|
   PullUp   |RC6/AN8             AN10/RB4|
   Butt_n->-|RC7/AN9               RB5/Rx|
            |RB7/Tx                   RB6|
            |____________________________|
			
  UART RB7, RB6 not used by this program		
 
  TTL to USB Serial Converter if used with Frizing serial monitor: 
                 FTDI TTL_232R-5V
          unconnected --- 6 RTS# green
  bbTx->- 1k resistor ->- 5 rxd  yellow TTL_232R-5V
  bbRx-<- 1k resistor -<- 4 txd  orange TTL_232R-5V		
          unconnected --- 3 VCC  red
          unconnected --- 2 CTS# brown
                  Gnd --- 1 GND  black					
*/

// code stored in the sketch: hello_blink.c
/* hello_blink.c  PICkit 2 breadboard LED + bitbanging com */ 
/* Blink with LED, receive char and printout loop count    */

/* B Knudsen Cc5x C-compiler - not ANSI-C */
#include <16F690.h>
#include <int16Cxx.h>
#pragma config |= 0x00D4 

/* FUNCTION PROTOTYPES */
void delay10( char );
void init_serial( void );
void putchar( char);
void printf(const char *string, char variable);

/* GLOBAL VARIABLES */
bit receiver_flag;   /* Signal-flag used by interrupt routine   */
char receiver_byte;  /* Transfer Byte used by interrupt routine */

/* INTERRUPT ROUTINE */
/* Interrupt routine - receiving chars at need */ 
#pragma origin 4
interrupt int_server( void ) /* the place for the interrupt routine */
{
  int_save_registers
  /* New interrupts are automaticaly disabled            */
  /* "Interrupt on change" at pin RA1 from PK2 UART-tool */
  
  if( PORTA.1 == 0 )  /* Interpret this as the startbit  */
    {  /* Receive one full character   */
      char bitCount, ti;
      /* delay 1,5 bit 156 usec at 4 MHz         */
      /* 5+28*5-1+1+2+9=156 without optimization */
      ti = 28; do ; while( --ti > 0); nop(); nop2();
      for( bitCount = 8; bitCount > 0 ; bitCount--)
       {
         Carry = PORTA.1;
         receiver_byte = rr( receiver_byte);  /* rotate carry */
         /* delay one bit 104 usec at 4 MHz       */
         /* 5+18*5-1+1+9=104 without optimization */ 
         ti = 18; do ; while( --ti > 0); nop(); 
        }
      receiver_flag = 1; /* A full character is now received */
    }
  RABIF = 0;    /* Reset the RABIF-flag before leaving   */
  int_restore_registers
  /* New interrupts are now enabled */
}


 /* MAIN PROGRAM */
void main( void)
{
    TRISC.0 = 0;   /* PORTC pin 0 output to LED     */
	TRISC.7 = 1;   /* PORTC pin 7 input from Button */
	ANSELH.1 = 0;  /* PORTC pin 7 not analog        */

    init_serial();
    char loopcounter=0;
	char speed = 100;
 
    receiver_flag=0;
  
    IOCA.1 = 1; /* PORTA.1 interrupt on change */
    RABIE =1;   /* interrupt on change         */
    GIE = 1;    /* interrupt enable            */
    
    delay10(100); /* wait one second */	
	printf("\r\nBlinks with LED\r\n",0); 
	printf("Receives char and then printout loop count.\r\n",0);
	printf("Fast blink if button is pressed.\r\n",0);
	
  while(1)
    {
	   if(!PORTC.7) speed=10; else speed=100; 
       delay10(speed);
	   PORTC.0 = 1; /* PORTC pin 0 "1" */
	   delay10(speed);
	   PORTC.0 = 0; /* PORTC pin 0 "0" */
	     if(receiver_flag) 
		   {
		     printf("\r\n", 0);
			 printf("%c ", receiver_byte);
		     printf("Loops = %u\r\n", loopcounter);
			 receiver_flag = 0;
		   }
	   loopcounter++;
    }
}




/* *********************************** */
/*            FUNCTIONS                */
/* *********************************** */

void delay10( char n)
/*
  Delays a multiple of 10 milliseconds using the TMR0 timer
  Clock : 4 MHz   => period T = 0.25 microseconds
  1 IS = 1 Instruction Cycle = 1 microsecond
  error: 0.16 percent
*/
{
    char i;

    OPTION = 7;
    do  {
        i = TMR0 + 39; /* 256 microsec * 39 = 10 ms */
        while ( i != TMR0)
            ;
    } while ( --n > 0);
}

void init_serial( void )  /* initialise PIC16F690 bitbang serialcom */
{
   ANSEL.0 = 0; /* No AD on RA0             */
   ANSEL.1 = 0; /* No AD on RA1             */
   PORTA.0 = 1; /* marking line             */
   TRISA.0 = 0; /* output to PK2 UART-tool  */
   TRISA.1 = 1; /* input from PK2 UART-tool */
   return;      
}

void putchar( char ch )  /* sends one char */
{
  char bitCount, ti;
  PORTA.0 = 0; /* set startbit */
  for ( bitCount = 10; bitCount > 0 ; bitCount-- )
   {
     /* delay one bit 104 usec at 4 MHz       */
     /* 5+18*5-1+1+9=104 without optimization */ 
     ti = 18; do ; while( --ti > 0); nop(); 
     Carry = 1;     /* stopbit                    */
     ch = rr( ch ); /* Rotate Right through Carry */
     PORTA.0 = Carry;
   }
  return;
}

void printf(const char *string, char variable) // printf look-alike
{
  char i, k, m, a, b;
  for(i = 0 ; ; i++)
   {
     k = string[i];
     if( k == '\0') break;   // at end of string
     if( k == '%')           // insert variable in string
      {
        i++;
        k = string[i];
        switch(k)
         {
           case 'd':         // %d  signed 8bit
             if( variable.7 ==1) putchar('-');
             else putchar(' ');
             if( variable > 127) variable = -variable;  // no break!
           case 'u':         // %u unsigned 8bit
             a = variable/100;
             putchar('0'+a); // print 100's
             b = variable%100;
             a = b/10;
             putchar('0'+a); // print 10's
             a = b%10;
             putchar('0'+a); // print 1's
             break;
           case 'x':         // %x HEX 8 bit
             static const char Hex_table[16] = "0123456789ABCDEF" ;
		     a = swap(variable);
             a = a & 0b0000.1111;
             b = Hex_table[a];
             putchar(b);
             a = variable & 0b0000.1111;
             b = Hex_table[a];
             putchar(b);
             break;
           case 'b':         // %b BINARY 8bit
             for( m = 0 ; m < 8 ; m++ )
              {
                if (variable.7 == 1) putchar('1');
                else putchar('0');
                variable = rl(variable);
               }
              break;
           case 'c':         // %c  'char'
             putchar(variable);
             break;
           case '%':
             putchar('%');
             break;
           default:          // not implemented
             putchar('!');
         }
      }
      else putchar(k);
   }
}





/* *********************************** */
/*            HARDWARE                 */
/* *********************************** */

/*
  Serial communication with PK2 UART-tool
  or used with TTL to USB Serial Converter
             _____________  _____________ 
            |             \/             |
      +5V---|Vdd        16F690        Vss|---Gnd
            |RA5            RA0/AN0/(PGD)|bbTx->- PK2 UART-tool
            |RA4/AN3            RA1/(PGC)|bbRx-<- PK2 UART-tool
            |RA3/!MCLR/(Vpp)  RA2/AN2/INT|
            |RC5/CCP                  RC0|->-LED0
            |RC4                      RC1|
            |RC3/AN7                  RC2|
   PullUp   |RC6/AN8             AN10/RB4|
   Butt_n->-|RC7/AN9               RB5/Rx|
            |RB7/Tx                   RB6|
            |____________________________|
			
  UART RB7, RB6 not used by this program		
 
  TTL to USB Serial Converter if used with Frizing serial monitor: 
                 FTDI TTL_232R-5V
          unconnected --- 6 RTS# green
  bbTx->- 1k resistor ->- 5 rxd  yellow TTL_232R-5V
  bbRx-<- 1k resistor -<- 4 txd  orange TTL_232R-5V		
          unconnected --- 3 VCC  red
          unconnected --- 2 CTS# brown
                  Gnd --- 1 GND  black					
*/

// code stored in the sketch: hello_blink.ino

/*  Compile with  PK2CC5X Tool chain
https://www.kth.se/social/course/IE1206/page/lab-programs-wiki-en/  */ 

/* hello_blink.c  PICkit 2 breadboard LED + bitbanging com    */
/* Program for testing components on breadboard               */ 
/* Blink with LED, serial menu LED on/off blink +/- Sw status */

/* B Knudsen Cc5x C-compiler - not ANSI-C */
#include <16F690.h>
#include <int16Cxx.h>
#pragma config |= 0x00D4 

/* FUNCTION PROTOTYPES */
void delay10( char );
void init_serial( void );
void putchar( char);
void printf(const char *string, char variable);

/* GLOBAL VARIABLES */
bit receiver_flag;   /* Signal-flag used by interrupt routine   */
char receiver_byte;  /* Transfer Byte used by interrupt routine */


/* INTERRUPT ROUTINE */
/* Interrupt routine - receiving chars at need */ 
#pragma origin 4
interrupt int_server( void ) /* the place for the interrupt routine */
{
  int_save_registers
  /* New interrupts are automaticaly disabled            */
  /* "Interrupt on change" at pin RA1 from PK2 UART-tool */
  
  if( PORTA.1 == 0 )  /* Interpret this as the startbit  */
    {  /* Receive one full character   */
      char bitCount, ti;
      /* delay 1,5 bit 156 usec at 4 MHz         */
      /* 5+28*5-1+1+2+9=156 without optimization */
      ti = 28; do ; while( --ti > 0); nop(); nop2();
      for( bitCount = 8; bitCount > 0 ; bitCount--)
       {
         Carry = PORTA.1;
         receiver_byte = rr( receiver_byte);  /* rotate carry */
         /* delay one bit 104 usec at 4 MHz       */
         /* 5+18*5-1+1+9=104 without optimization */ 
         ti = 18; do ; while( --ti > 0); nop(); 
        }
      receiver_flag = 1; /* A full character is now received */
    }
  RABIF = 0;    /* Reset the RABIF-flag before leaving   */
  int_restore_registers
  /* New interrupts are now enabled */
}



 /* MAIN PROGRAM */

void main( void)
{
    /* Initialisations */

  TRISC.0 = 0;   /* PORTC pin 0 output to LED     */
  TRISC.7 = 1;   /* PORTC pin 7 input from Button */
  ANSELH.1 = 0;  /* PORTC pin 7 not analog        */

  init_serial();
  char speed = 100;
  char period;
  char choice;
  bit blink=1;
  receiver_flag=0;
  
  IOCA.1 = 1; /* PORTA.1 interrupt on change */
  RABIE =1;   /* interrupt on change         */
  GIE = 1;    /* interrupt enable            */
    
    /* Main loop  */

  while(1)
   {
     if( receiver_flag ) /* Character received? */ 
      {
        choice = receiver_byte;
        receiver_flag = 0; /* Character now taken */
        /* menu alternatives */
        switch (choice)
         {
          case 'l':
          case 'L':
            printf("\r\n%c LED ON\r\n", choice);
            PORTC.0 = 1; /* PORTC pin 0 "1" */
            blink=0;
            break;
          case 'o':
          case 'O':
            printf("\r\n%c LED OFF\r\n", choice);
            PORTC.0 = 0; /* PORTC pin 0 "0" */
            blink=0;
            break;
          case 'b':
          case 'B':
            blink=1;
            printf("\r\n%c LED BLINK\r\n", choice);
            break;
          case 'S':
          case 's':
            if(!PORTC.7) printf("\r\n%c Switch is ON/pressed\r\n", choice);
            else printf("\r\n%c Switch is OFF/unpressed\r\n", choice);
            break;
          case '-':
            if(period > 20) period -=10;
            else period = 10;
            printf("\r\n%c ", choice);
            printf("Dec delay %u\r\n", period);
            blink = 1;
            break;
          case '+':
            if(period < 240) period +=10;
            else period = 250;
            printf("\r\n%c ", choice);
            printf("Inc delay %u\r\n", period);
            blink = 1;
            break;
          default:
            printf("\r\n%c (L)ed On, led (O)ff, led (B)link, ",choice);
            printf("(S)witch, delay (+),(-)\r\n",0);
         }
      }

      /* Button action fast blink */
 	  if(PORTC.7) speed = period; else speed = 10;
	  
      /* blink the led with different period */
	  if( blink )
        {  
          delay10(speed);
    	    PORTC.0 = 1; /* PORTC pin 0 "1" */
    	    delay10(speed);
    	    PORTC.0 = 0; /* PORTC pin 0 "0" */
        }

   }

}




/* *********************************** */
/*            FUNCTIONS                */
/* *********************************** */

void delay10( char n)
/*
  Delays a multiple of 10 milliseconds using the TMR0 timer
  Clock : 4 MHz   => period T = 0.25 microseconds
  1 IS = 1 Instruction Cycle = 1 microsecond
  error: 0.16 percent
*/
{
    char i;

    OPTION = 7;
    do  {
          i = TMR0 + 39; /* 256 microsec * 39 = 10 ms */
          while ( i != TMR0)
            ;
        } while ( --n > 0);
}


void init_serial( void )  /* initialise PIC16F690 bitbang serialcom */
{
   ANSEL.0 = 0; /* No AD on RA0             */
   ANSEL.1 = 0; /* No AD on RA1             */
   PORTA.0 = 1; /* marking line             */
   TRISA.0 = 0; /* output to PK2 UART-tool  */
   TRISA.1 = 1; /* input from PK2 UART-tool */
   return;      
}



void putchar( char ch )  /* sends one char */
{
  char bitCount, ti;
  PORTA.0 = 0; /* set startbit */
  for ( bitCount = 10; bitCount > 0 ; bitCount-- )
   {
     /* delay one bit 104 usec at 4 MHz       */
     /* 5+18*5-1+1+9=104 without optimization */ 
     ti = 18; do ; while( --ti > 0); nop(); 
     Carry = 1;     /* stopbit                    */
     ch = rr( ch ); /* Rotate Right through Carry */
     PORTA.0 = Carry;
   }
  return;
}



void printf(const char *string, char variable) // printf look-alike
{
  char i, k, m, a, b;
  for(i = 0 ; ; i++)
   {
     k = string[i];
     if( k == '\0') break;   // at end of string

     if( k == '%')           // insert variable in string
      {
        i++;
        k = string[i];
        switch(k)
         {
           case 'd':         // %d  signed 8bit
             if( variable.7 ==1) putchar('-');
             else putchar(' ');
             if( variable > 127) variable = -variable;  // no break!
           case 'u':         // %u unsigned 8bit
             a = variable/100;
             putchar('0'+a); // print 100's
             b = variable%100;
             a = b/10;
             putchar('0'+a); // print 10's
             a = b%10;
             putchar('0'+a); // print 1's
             break;
           case 'x':         // %x HEX 8 bit
             static const char Hex_table[16] = "0123456789ABCDEF" ;
             a = swap(variable);
             a = a & 0b0000.1111;
             b = Hex_table[a];
             putchar(b);
             a = variable & 0b0000.1111;
             b = Hex_table[a];
             putchar(b);
             break;
           case 'b':         // %b BINARY 8bit
             for( m = 0 ; m < 8 ; m++ )
              {
                if (variable.7 == 1) putchar('1');
                else putchar('0');
                variable = rl(variable);
              }
             break;
           case 'c':         // %c  'char'
             putchar(variable);
             break;
           case '%':
             putchar('%');
             break;
           default:          // not implemented
             putchar('!');
         }
       }
      else putchar(k);
   }

}







/* *********************************** */
/*            HARDWARE                 */
/* *********************************** */

/*
  Serial communication with PK2 UART-tool
  or used with TTL to USB Serial Converter
             _____________  _____________ 
            |             \/             |
      +5V---|Vdd        16F690        Vss|---Gnd
            |RA5            RA0/AN0/(PGD)|bbTx->- PK2 UART-tool
            |RA4/AN3            RA1/(PGC)|bbRx-<- PK2 UART-tool
            |RA3/!MCLR/(Vpp)  RA2/AN2/INT|
            |RC5/CCP                  RC0|->-LED0
            |RC4                      RC1|
            |RC3/AN7                  RC2|
   PullUp   |RC6/AN8             AN10/RB4|
   Butt_n->-|RC7/AN9               RB5/Rx|
            |RB7/Tx                   RB6|
            |____________________________|
			
  UART RB7, RB6 not used by this program		
 
  TTL to USB Serial Converter if used with Frizing serial monitor: 
                 FTDI TTL_232R-5V
          unconnected --- 6 RTS# green
  bbTx->- 1k resistor ->- 5 rxd  yellow TTL_232R-5V
  bbRx-<- 1k resistor -<- 4 txd  orange TTL_232R-5V		
          unconnected --- 3 VCC  red
          unconnected --- 2 CTS# brown
                  Gnd --- 1 GND  black					
*/

// code stored in the sketch: hello_blink_TMP.ino

/*  Compile with  PK2CC5X Tool chain
https://github.com/willsandy/Fritzing-PK2-Cc5x  */ 

/* hello_blink.c  PICkit 2 breadboard LED + bitbanging com    */
/* Program for testing components on breadboard               */ 
/* Blink with LED, serial menu LED on/off blink +/- Sw status */

/* B Knudsen Cc5x C-compiler - not ANSI-C */
#include <16F690.h>
#include <int16Cxx.h>
#pragma config |= 0x00D4 

/* FUNCTION PROTOTYPES */
void delay10( char );
void init_serial( void );
void putchar( char);
void printf(const char *string, char variable);

/* GLOBAL VARIABLES */
bit receiver_flag;   /* Signal-flag used by interrupt routine   */
char receiver_byte;  /* Transfer Byte used by interrupt routine */


/* INTERRUPT ROUTINE */
/* Interrupt routine - receiving chars at need */ 
#pragma origin 4
interrupt int_server( void ) /* the place for the interrupt routine */
{
  int_save_registers
  /* New interrupts are automaticaly disabled            */
  /* "Interrupt on change" at pin RA1 from PK2 UART-tool */
  
  if( PORTA.1 == 0 )  /* Interpret this as the startbit  */
    {  /* Receive one full character   */
      char bitCount, ti;
      /* delay 1,5 bit 156 usec at 4 MHz         */
      /* 5+28*5-1+1+2+9=156 without optimization */
      ti = 28; do ; while( --ti > 0); nop(); nop2();
      for( bitCount = 8; bitCount > 0 ; bitCount--)
       {
         Carry = PORTA.1;
         receiver_byte = rr( receiver_byte);  /* rotate carry */
         /* delay one bit 104 usec at 4 MHz       */
         /* 5+18*5-1+1+9=104 without optimization */ 
         ti = 18; do ; while( --ti > 0); nop(); 
        }
      receiver_flag = 1; /* A full character is now received */
    }
  RABIF = 0;    /* Reset the RABIF-flag before leaving   */
  int_restore_registers
  /* New interrupts are now enabled */
}



 /* MAIN PROGRAM */

void main( void)
{
    /* Initialisations */

  TRISC.0 = 0;   /* PORTC pin 0 output to LED     */
	TRISC.7 = 1;   /* PORTC pin 7 input from Button */
	ANSELH.1 = 0;  /* PORTC pin 7 not analog        */

  init_serial();
	char speed = 100;
  char period;
	char choice;
  bit blink=1;
  receiver_flag=0;
  
  IOCA.1 = 1; /* PORTA.1 interrupt on change */
  RABIE =1;   /* interrupt on change         */
  GIE = 1;    /* interrupt enable            */
    
    /* Main loop  */

	while(1)
   {
     if( receiver_flag ) /* Character received? */ 
      {
        choice = receiver_byte;
        receiver_flag = 0; /* Character now taken */
		/* menu alternatives */
        switch (choice)
         {
          case 'l':
          case 'L':
            printf("\r\n%c LED ON\r\n", choice);
	          PORTC.0 = 1; /* PORTC pin 0 "1" */
            blink=0;
            break;
          case 'o':
          case 'O':
            printf("\r\n%c LED OFF\r\n", choice);
  	        PORTC.0 = 0; /* PORTC pin 0 "0" */
            blink=0;
            break;
          case 'b':
          case 'B':
            blink=1;
            printf("\r\n%c LED BLINK\r\n", choice);
            break;
          case 'S':
          case 's':
	          if(!PORTC.7) printf("\r\n%c Switch is ON/pressed\r\n", choice);
            else printf("\r\n%c Switch is OFF/unpressed\r\n", choice);
            break;
          case '-':
            if(period > 20) period -=10;
            else period = 10;
            printf("\r\n%c ", choice);
            printf("Dec delay %u\r\n", period);
		        blink = 1;
            break;
          case '+':
            if(period < 240) period +=10;
            else period = 250;
            printf("\r\n%c ", choice);
            printf("Inc delay %u\r\n", period);
		        blink = 1;
            break;
          default:
            printf("\r\n%c (L)ed On, led (O)ff, led (B)link, ",choice);
		        printf("(S)witch, delay (+),(-)\r\n",0);
         }
      }

      /* Button action fast blink */
 	  if(PORTC.7) speed = period; else speed = 10;
	  
      /* blink the led with different period */
	  if( blink )
        {  
          delay10(speed);
    	    PORTC.0 = 1; /* PORTC pin 0 "1" */
    	    delay10(speed);
    	    PORTC.0 = 0; /* PORTC pin 0 "0" */
        }

   }

}




/* *********************************** */
/*            FUNCTIONS                */
/* *********************************** */

void delay10( char n)
/*
  Delays a multiple of 10 milliseconds using the TMR0 timer
  Clock : 4 MHz   => period T = 0.25 microseconds
  1 IS = 1 Instruction Cycle = 1 microsecond
  error: 0.16 percent
*/
{
    char i;

    OPTION = 7;
    do  {
          i = TMR0 + 39; /* 256 microsec * 39 = 10 ms */
          while ( i != TMR0)
            ;
        } while ( --n > 0);
}


void init_serial( void )  /* initialise PIC16F690 bitbang serialcom */
{
   ANSEL.0 = 0; /* No AD on RA0             */
   ANSEL.1 = 0; /* No AD on RA1             */
   PORTA.0 = 1; /* marking line             */
   TRISA.0 = 0; /* output to PK2 UART-tool  */
   TRISA.1 = 1; /* input from PK2 UART-tool */
   return;      
}



void putchar( char ch )  /* sends one char */
{
  char bitCount, ti;
  PORTA.0 = 0; /* set startbit */
  for ( bitCount = 10; bitCount > 0 ; bitCount-- )
   {
     /* delay one bit 104 usec at 4 MHz       */
     /* 5+18*5-1+1+9=104 without optimization */ 
     ti = 18; do ; while( --ti > 0); nop(); 
     Carry = 1;     /* stopbit                    */
     ch = rr( ch ); /* Rotate Right through Carry */
     PORTA.0 = Carry;
   }
  return;
}



void printf(const char *string, char variable) // printf look-alike
{
  char i, k, m, a, b;
  for(i = 0 ; ; i++)
   {
     k = string[i];
     if( k == '\0') break;   // at end of string

     if( k == '%')           // insert variable in string
      {
        i++;
        k = string[i];
        switch(k)
         {
           case 'd':         // %d  signed 8bit
             if( variable.7 ==1) putchar('-');
             else putchar(' ');
             if( variable > 127) variable = -variable;  // no break!
           case 'u':         // %u unsigned 8bit
             a = variable/100;
             putchar('0'+a); // print 100's
             b = variable%100;
             a = b/10;
             putchar('0'+a); // print 10's
             a = b%10;
             putchar('0'+a); // print 1's
             break;
           case 'x':         // %x HEX 8 bit
             static const char Hex_table[16] = "0123456789ABCDEF" ;
             a = swap(variable);
             a = a & 0b0000.1111;
             b = Hex_table[a];
             putchar(b);
             a = variable & 0b0000.1111;
             b = Hex_table[a];
             putchar(b);
             break;
           case 'b':         // %b BINARY 8bit
             for( m = 0 ; m < 8 ; m++ )
              {
                if (variable.7 == 1) putchar('1');
                else putchar('0');
                variable = rl(variable);
              }
             break;
           case 'c':         // %c  'char'
             putchar(variable);
             break;
           case '%':
             putchar('%');
             break;
           default:          // not implemented
             putchar('!');
         }
       }
      else putchar(k);
   }

}







/* *********************************** */
/*            HARDWARE                 */
/* *********************************** */

/*
  Serial communication with PK2 UART-tool
  or used with TTL to USB Serial Converter
             _____________  _____________ 
            |             \/             |
      +5V---|Vdd        16F690        Vss|---Gnd
            |RA5            RA0/AN0/(PGD)|bbTx->- PK2 UART-tool
            |RA4/AN3            RA1/(PGC)|bbRx-<- PK2 UART-tool
            |RA3/!MCLR/(Vpp)  RA2/AN2/INT|
            |RC5/CCP                  RC0|->-LED0
            |RC4                      RC1|
            |RC3/AN7                  RC2|
   PullUp   |RC6/AN8             AN10/RB4|
   Butt_n->-|RC7/AN9               RB5/Rx|
            |RB7/Tx                   RB6|
            |____________________________|
			
  UART RB7, RB6 not used by this program		
 
  TTL to USB Serial Converter if used with Frizing serial monitor: 
                 FTDI TTL_232R-5V
          unconnected --- 6 RTS# green
  bbTx->- 1k resistor ->- 5 rxd  yellow TTL_232R-5V
  bbRx-<- 1k resistor -<- 4 txd  orange TTL_232R-5V		
          unconnected --- 3 VCC  red
          unconnected --- 2 CTS# brown
                  Gnd --- 1 GND  black					
*/

// code stored in the sketch: microwave_timer.ino
/*	name_program.c  */
/*	Taqui Shah and Viktor Vitek,
	Timer that ticks down after being set a time. 
	Much like a mircowave-timer.*/
/*	LCD two line 16 characthers display         
	Potensometer*/
#include "16F690.h"
#pragma config |= 0x00D4 
/*	I/O-pin definitions                               */ 
/*	change if you need a pin for a different purpose  */
#pragma bit RS  @ PORTB.4
#pragma bit EN  @ PORTB.6
#pragma bit D7  @ PORTC.3
#pragma bit D6  @ PORTC.2
#pragma bit D5  @ PORTC.1
#pragma bit D4  @ PORTC.0
/*	The right value for the potensometer*/ 
#define SCALE_FACTOR 49 //	This gives us 50-0 minutes range
/*	Calling fucntions  */
void delay(char); 
void ADinit(void);
void lcd_init(void); 
void lcd_putchar(char);	
long potentiometer(void);
char modulo(unsigned long dividend, long divisor);
void lcd_putline(char start, const char * text, char variable_1, char variable_2, char variable_3, char variable_4);


void main(void)
{
    /*	init of I/O-pin direction in/out definitions	*/
	ANSEL	= 0; 	//  PORTC digital I/O
	ANSELH	= 0;
	TRISC	= 0b1111.0000;  /* RC3,2,1,0 out*/
    TRISB.4 = 0;	/*	RB4, RB6 out, Potensometer?*/
    TRISB.6 = 0;	
	TRISB.7 = 1;	/*Initialisering av knappen, weak-pullup fix*/
	OPTION.7= 0;
	WPUB.7	= 1;
	
	/*	init of lcd	and AD converter*/
	lcd_init();
	ADinit();
	/*	init of variables	*/
	int		temp_variable = 0;
	char	minute_tens_diget = '0',	minute_ones_diget = '0',	second_tens_diget = '0',	second_ones_diget = '0',	i; //sign to authorize the tick, i for loops.
	unsigned int	time_minutes = 0,	time_seconds = 1;
	
	/*	Before loop	*/
	
	time_minutes = potentiometer(); // Set start-time
	
	/*	*********	*/
	/*	main_loop	*/
	/*	*********	*/
	while(1){
	
		/*	LCD-clear	*/
		RS = 0;  
		lcd_putchar(1);  
		RS = 1;

		
		/*	************	*/
		/*	    Tick      	*/
		/*	************	*/
		
		if(time_minutes!=0 || time_seconds!=0) //NAND
		{
			time_seconds--;
			
			
			/*	*******************	*/
			/*	int to char convert	*/
			/*  ******************* */
			
			/*	Seconds				*/
			
			second_ones_diget = modulo(time_seconds, 10) + '0'; // Modulo will get the ones diget. "+ '0'" so we start in the correct place in the ASCII-table.  
			
			second_tens_diget = '0'; // Correct char-value to start with.
			if(time_seconds >= 10) // If seconds is less than ten, then the tens diget will be 0.
			{
				temp_variable = time_seconds / 10; // But if it's equal or more than ten, then the tens diget will be correct. xy/10=x (Rounding correct because of the nature of int.)
				second_tens_diget += temp_variable; // Temporary variable because of slow processor. 
			}
			
			
			/*	Minutes				*/
			
			minute_ones_diget = modulo(time_minutes, 10) + '0'; // Same as seconds.
			
			minute_tens_diget = '0';
			if(time_minutes >= 10)
			{
				temp_variable = time_minutes / 10;
				minute_tens_diget += temp_variable;
			}
			if(time_minutes > 59)
			{
				time_minutes = 0;
			}
			
			//	Display numbers on LCD.
			lcd_putline(0, "%c%c:%c%c", minute_tens_diget, minute_ones_diget, second_tens_diget, second_ones_diget);	
			
			// Delay a second
			for(i = 0; i < 5; i++){ 
				delay(100);  
			}
			
			/* When the button is pressed it gets inside the if statement. Then it waits for the user to let go of the button*/
			if(PORTB.7 == 1) 
			{
				while(PORTB.7 == 1);
				time_minutes = potentiometer();
				time_seconds = 1; //time_seconds is one do to the decrementation that occurs in the begining of the loop.
			}
			
			//Checks if seconds is 0, if so count down new minute. This is last because of unsigned int can't be negative and we want to show 00
			if(time_seconds == 0 && time_minutes != 0)
			{
				time_seconds = 60;
				time_minutes--;
			}			
		}else{// If timer is 00:00, then done!
				lcd_putline(0, "DONE!", 0, 0, 0, 0); 
				while(PORTB.7 == 0); // Wait for button to restart.
				delay(10);
				while(PORTB.7 == 1);
				time_minutes = potentiometer();
				time_seconds = 1;
			}	
		}
		//Exit
		while(1) nop();
	}

	
	
/* *********************************** */
/*            FUNCTIONS                */
/* *********************************** */


 char   modulo(unsigned long dividend, long divisor){
 /* 
	Classic modulo function
	see more @https://en.wikipedia.org/wiki/Modulo_operation
*/
	while(dividend >= divisor)
	{
		dividend -= divisor;
	}
	return dividend;
 }
 
 
/* 
	Predone LCD-functions
*/ 

void ADinit(void)
{
	// AD setup 
	ANSEL.2 = 1; // RA2 AN2 analog configurated
	TRISA.2=1;   // AN2 input

	ADCON1 = 0b0.101.0000; // AD conversion clock 'fosc/16'

	/* 
	 1.x.xxxx.x.x  ADRESH:ADRESL is 10 bit right justified
	 x.0.xxxx.x.x  Vref is Vdd
	 x.x.0010.x.x  Channel (AN2) 
	 x.x.xxxx.0.x  Go/!Done - start from program later
	 x.x.xxxx.x.1  Enable AD-converter
	*/
	ADCON0 = 0b1.0.0010.0.1; 
}

void lcd_putchar(char data)
{
	// must set LCD-mode before calling this function!
	// RS = 1 LCD in character-mode
	// RS = 0 LCD in command-mode
	// upper Nybble
	D7 = data.7;
	D6 = data.6;
	D5 = data.5;
	D4 = data.4;
	EN = 0;
	nop();
	EN = 1;
	delay(5);
	// lower Nybble
	D7 = data.3;
	D6 = data.2;
	D5 = data.1;
	D4 = data.0;
	EN = 0;
	nop();
	EN = 1;
	delay(5);
}

void lcd_putline(char start, const char * text,char variable_1, char variable_2, char variable_3, char variable_4)
{
/* 
	Changde to 4 variables.
*/
	RS = 0;  // LCD in command-mode
	lcd_putchar(start);  // move to text position
	RS = 1;  // LCD in character-mode
	char i, k, counter=0, variable=0,a,m,b;

	for(i = 0 ; ; i++)
	{
		k = text[i];
		if( k == '\0') return;
		if( k == '%')           // insert variable in string
		{
			i++;
			k = text[i];
			switch(counter) {

				case 0:
					variable = variable_1;
					break;
				case 1:
					variable = variable_2;
					break;
				case 2:
					variable = variable_3;
					break;
				case 3:
					variable = variable_4;
					break;
				/* We have 4 case statements */

			};
			counter++;
			switch(k)
			{
				case 'd':         // %d  signed 8bit
				if( variable.7 ==1) lcd_putchar('-');
				else lcd_putchar(' ');
				if( variable > 127) variable = -variable;  // no break!
				case 'u':         // %u unsigned 8bit
					a = variable/100;
					lcd_putchar('0'+a); // print 100's
					b = variable%100;
					a = b/10;
					lcd_putchar('0'+a); // print 10's
					a = b%10;
					lcd_putchar('0'+a); // print 1's
					break;
				case 'b':         // %b BINARY 8bit
					for( m = 0 ; m < 8 ; m++ )
					{
						if (variable.7 == 1) lcd_putchar('1');
						else lcd_putchar('0');
						variable = rl(variable);
					}
					break;
				case 'c':         // %c  'char'
					lcd_putchar(variable);
					break;
				case '%':
					lcd_putchar('%');
					break;
				default:          // not implemented
					lcd_putchar('!');
			}
		}else	lcd_putchar(k); // found end of string
	}
	return;  
}
long potentiometer(void){
unsigned long advalue, potens=0;
char show_minute_tens=0, show_minute_ones=0;
int  i;
delay(100); 
// Loop
while(1)
{
	show_minute_tens = '0';
	show_minute_ones = '0';
	// LED Sampling indicator
	// Now measure the Voltage [V]  
	GO = 1;         // start AD
	while(GO);    // wait for done
	advalue  = ADRESH * 256;    // read result 10 bit
	advalue += ADRESL;
	// 1024 -> 50000 
	// multiply with integer scalefactor
	advalue *= SCALE_FACTOR;  
	potens   = advalue / 1000; // Potens becomes 50 when voltage is 5V which indicates the amount of minutes
	show_minute_tens = modulo(potens, 10); // Modulo 10 tells us the first digit of the number potens
	show_minute_ones = potens / 10; // Tells us the second digit in the potens variable
	show_minute_tens+= '0';// Creates a char from the first digit
	show_minute_ones+= '0';// Creates a char from the second digit
	lcd_putline(0, "%c%c Antal Minuter", show_minute_ones, show_minute_tens, 0, 0); //displays the digits
	for(i = 0; i < 10; i++)
	{
		delay(10);
		
	}// Delay is created
	RS = 0;  
	lcd_putchar(1);  
	RS = 1;
	// Clears the screen
	if(PORTB.7 == 1)
	{
		while(PORTB.7 == 1); // Breaks the loop when customer is finished picking amount of minutes
		break;
	}
	
}


return potens;

}

void delay(char millisec)
/* 
  Delays a multiple of 1 milliseconds at 4 MHz (16F690 internal clock)
  using the TMR0 timer 
*/
{
    OPTION = 2;  /* prescaler divide by 8        */
    do  {
        TMR0 = 0;
        while ( TMR0 < 125)   /* 125 * 8 = 1000  */
            ;
    } while ( -- millisec > 0);
}

void lcd_init( void ) // must be run once before using the display
{
  delay(40);  // give LCD time to settle
  RS = 0;     // LCD in command-mode
  lcd_putchar(0b0011.0011); /* LCD starts in 8 bit mode          */
  lcd_putchar(0b0011.0010); /* change to 4 bit mode              */
  lcd_putchar(0b00101000);  /* two line (8+8 chars in the row)   */ 
  lcd_putchar(0b00001100);  /* display on, cursor off, blink off */
  lcd_putchar(0b00000001);  /* display clear                     */
  lcd_putchar(0b00000110);  /* increment mode, shift off         */
  RS = 1;    // LCD in character-mode
             // initialization is done!
}

/* *********************************** */
/*            HARDWARE                 */
/* *********************************** */

/*
         ___________  ___________
        |           \/           |
  +5V---|Vdd     16F690       Vss|---GND
        |RA5        RA0/AN0/(PGD)|
        |RA4            RA1/(PGC)|
        |RA3/!MCLR/(Vpp)  RA2/INT|->- Potentiometer
        |RC5/CCP              RC0|->-D4
        |RC4                  RC1|->-D5
  D7 -<-|RC3                  RC2|->-D6
        |RC6                  RB4|->- RS
        |RC7               RB5/Rx|
Butt -<-|RB7/Tx               RB6|->- EN
        |________________________| 

*/

/*
           LCD two lines, Line length 16 characters
           Internal ic: HD44780A00		   
           _______________
          |               |
          |         Vss  1|--- GND  
          |         Vdd  2|--- +5V
          |    Contrast  3|-<- Pot
          |          RS  4|-<- RB4
          |      RD/!WR  5|--- 0, GND
          |          EN  6|-<- RB6
          |          D0  7|
          |          D1  8|
          |          D2  9|
          |          D3 10|
          |          D4 11|-<- RC0
          |          D5 12|-<- RC1 
          |          D6 13|-<- RC2
          |          D7 14|-<- RC3 
          |_______________|						  
*/

// code stored in the sketch: microwave_timer_final.ino
/*	microwave_timer.c  */
/*	Taqui Shah and Viktor Vitek,
	Timer that ticks down after being set a time. 
	Much like a mircowave-timer.*/
/*	LCD two line 16 characthers display  
	Compiler CC5x - not ANSI-C
	Potensometer*/
#include "16F690.h"
#pragma config |= 0x00D4 
/*	I/O-pin definitions                               */ 
/*	change if you need a pin for a different purpose  */
#pragma bit RS  @ PORTB.4
#pragma bit EN  @ PORTB.6
#pragma bit D7  @ PORTC.3
#pragma bit D6  @ PORTC.2
#pragma bit D5  @ PORTC.1
#pragma bit D4  @ PORTC.0
/*	The right value for the potensometer*/ 
#define SCALE_FACTOR 49 //	This gives us 50-0 minutes range
/*	init fucntions  */
void delay(char); 
void ADinit(void);
void lcd_init(void); 
void lcd_putchar(char);	
long potentiometer(void);
char modulo(unsigned long dividend, long divisor);
void lcd_putline(char start, const char * text, char variable_1, char variable_2, char variable_3, char variable_4);


void main(void)
{
    /*	init of I/O-pin direction in/out definitions	*/
	ANSEL	= 0; 	//  PORTC digital I/O
	ANSELH	= 0;
	TRISC	= 0b1111.0000;  /* RC3,2,1,0 out*/
    TRISB.4 = 0;	/*	RB4, RB6 out*/
    TRISB.6 = 0;	
	TRISB.7 = 1;	/*Initialisering av knappen, weak-pullup fix*/
	OPTION.7= 0;
	WPUB.7	= 1;
	
	/*	init of lcd	and AD converter*/
	lcd_init();
	ADinit();
	/*	init of variables	*/
	int		temp_variable = 0;
	char	minute_tens_diget = '0',	minute_ones_diget = '0',	second_tens_diget = '0',	second_ones_diget = '0',	i;
	unsigned int	time_minutes = 0,	time_seconds = 1;
	
	/*	Before loop	*/
	
	time_minutes = potentiometer(); // Set start-time
	
	/*	*********	*/
	/*	main_loop	*/
	/*	*********	*/
	while(1){
	
		/*	LCD-clear	*/
		RS = 0;  
		lcd_putchar(1);  
		RS = 1;

		
		/*	************	*/
		/*	  Control      	*/
		/*	************	*/
		
		if(time_minutes!=0 || time_seconds!=0) //NAND, if both are true, then go to else (this statement outputs 0)
		{
		
			time_seconds--;
			
			/*	*******************	*/
			/*	int to char convert	*/
			/*  ******************* */
			
			/*	Seconds				*/
			second_ones_diget = modulo(time_seconds, 10) + '0'; // Modulo will get the ones diget. "+ '0'" so we start in the correct place in the ASCII-table.  
			
			second_tens_diget = '0'; // Correct char-value to start with.
			if(time_seconds >= 10) // If seconds is less than ten, then the tens diget will be 0.
			{
				temp_variable = time_seconds / 10; // But if it's equal or more than ten, then the tens diget will be correct. xy/10=x (Rounding correct because of the nature of int.)
				second_tens_diget += temp_variable; // Temporary variable because of slow processor. 
			}
			
			/*	Minutes				*/
			minute_ones_diget = modulo(time_minutes, 10) + '0'; // Same as seconds.
			
			minute_tens_diget = '0';
			if(time_minutes >= 10)
			{
				temp_variable = time_minutes / 10;
				minute_tens_diget += temp_variable;
			}
			if(time_minutes > 59)
			{
				time_minutes = 0;
			}
			
			//	Display numbers on LCD.
			lcd_putline(0, "%c%c:%c%c", minute_tens_diget, minute_ones_diget, second_tens_diget, second_ones_diget);	
			
			// Delay a second
			for(i = 0; i < 9; i++){ 
				delay(100);  
			}
			
			/* When the button is pressed it gets inside the if statement. Then it waits for the user to let go of the button*/
			if(PORTB.7 == 1) 
			{
				while(PORTB.7 == 1);
				time_minutes = potentiometer();
				time_seconds = 1; //time_seconds is one do to the decrementation that occurs in the begining of the loop.
			}
			
			//Checks if seconds is 0, if so count down new minute. This is last because of unsigned int can't be negative and we want to show 00
			if(time_seconds == 0 && time_minutes != 0)
			{
				time_seconds = 60;
				time_minutes--;
			}			
		}else{// If timer is 00:00, then done!
				lcd_putline(0, "DONE!", 0, 0, 0, 0); 
				while(PORTB.7 == 0); // Wait for button to restart.
				delay(10);
				while(PORTB.7 == 1);
				time_minutes = potentiometer();
				time_seconds = 1;
			}	
		}
		//Exit
		while(1) nop();
	}

	
	
/* *********************************** */
/*            FUNCTIONS                */
/* *********************************** */

char   modulo(unsigned long dividend, long divisor)
{
/* 
	Classic modulo function
	see more @https://en.wikipedia.org/wiki/Modulo_operation
*/
	while(dividend >= divisor)
	{
		dividend -= divisor;
	}
	return dividend;
}


/* 
	Most borrowed from the already done potentiometer function, which is the ADvalue variables.
	We've changed the SCALEFACTOR and we also added display functions to show different values to the LCD, in this function.
	Also included the button. To break the while loop if pressed.
*/ 

long potentiometer(void)
{
	unsigned long advalue, potens=0;
	char show_minute_tens=0, show_minute_ones=0;
	int  i;
	delay(100); 
	
	// Loop
	while(1)
	{
		show_minute_tens = '0';
		show_minute_ones = '0';
		// LED Sampling indicator
		// Now measure the Voltage [V]  
		GO = 1;         // start AD
		while(GO);    // wait for done
		advalue  = ADRESH * 256;    // read result 10 bit
		advalue += ADRESL;
		// 1024 -> 50000 
		// multiply with integer scalefactor
		advalue *= SCALE_FACTOR;  
		potens   = advalue / 1000; // Potens becomes 50 when voltage is 5V which indicates the amount of minutes
		
		show_minute_tens = modulo(potens, 10); // Modulo 10 tells us the first digit of the number potens
		show_minute_ones = potens / 10; // Tells us the second digit in the potens variable
		show_minute_tens+= '0';// Creates a char from the first digit
		show_minute_ones+= '0';// Creates a char from the second digit
		lcd_putline(0, "%c%c Antal Minuter", show_minute_ones, show_minute_tens, 0, 0); //displays the digits
		// Delay is created
		for(i = 0; i < 10; i++)
		{
			delay(10);
		}
		
		// Clears the screen
		RS = 0;  
		lcd_putchar(1);  
		RS = 1;
		
		// Breaks the loop when customer is finished picking amount of minutes
		if(PORTB.7 == 1)
		{
			while(PORTB.7 == 1); 
			break;
		}
	}
	return potens;
}
 

/* 
	Predone LCD-functions
*/ 

void ADinit(void)
{
	// AD setup 
	ANSEL.2 = 1; // RA2 AN2 analog configurated
	TRISA.2=1;   // AN2 input

	ADCON1 = 0b0.101.0000; // AD conversion clock 'fosc/16'

	/* 
	 1.x.xxxx.x.x  ADRESH:ADRESL is 10 bit right justified
	 x.0.xxxx.x.x  Vref is Vdd
	 x.x.0010.x.x  Channel (AN2) 
	 x.x.xxxx.0.x  Go/!Done - start from program later
	 x.x.xxxx.x.1  Enable AD-converter
	*/
	ADCON0 = 0b1.0.0010.0.1; 
}

void lcd_putchar(char data)
{
	// must set LCD-mode before calling this function!
	// RS = 1 LCD in character-mode
	// RS = 0 LCD in command-mode
	// upper Nybble
	D7 = data.7;
	D6 = data.6;
	D5 = data.5;
	D4 = data.4;
	EN = 0;
	nop();
	EN = 1;
	delay(5);
	// lower Nybble
	D7 = data.3;
	D6 = data.2;
	D5 = data.1;
	D4 = data.0;
	EN = 0;
	nop();
	EN = 1;
	delay(5);
}

void lcd_putline(char start, const char * text,char variable_1, char variable_2, char variable_3, char variable_4)
{
/* 
	Changde to 4 variables.
*/
	RS = 0;  // LCD in command-mode
	lcd_putchar(start);  // move to text position
	RS = 1;  // LCD in character-mode
	char i, k, counter=0, variable=0,a,m,b;

	for(i = 0 ; ; i++)
	{
		k = text[i];
		if( k == '\0') return;
		if( k == '%')           // insert variable in string
		{
			i++;
			k = text[i];
			switch(counter) {

				case 0:
					variable = variable_1;
					break;
				case 1:
					variable = variable_2;
					break;
				case 2:
					variable = variable_3;
					break;
				case 3:
					variable = variable_4;
					break;
				/* We have 4 case statements */

			};
			counter++;
			switch(k)
			{
				case 'd':         // %d  signed 8bit
				if( variable.7 ==1) lcd_putchar('-');
				else lcd_putchar(' ');
				if( variable > 127) variable = -variable;  // no break!
				case 'u':         // %u unsigned 8bit
					a = variable/100;
					lcd_putchar('0'+a); // print 100's
					b = variable%100;
					a = b/10;
					lcd_putchar('0'+a); // print 10's
					a = b%10;
					lcd_putchar('0'+a); // print 1's
					break;
				case 'b':         // %b BINARY 8bit
					for( m = 0 ; m < 8 ; m++ )
					{
						if (variable.7 == 1) lcd_putchar('1');
						else lcd_putchar('0');
						variable = rl(variable);
					}
					break;
				case 'c':         // %c  'char'
					lcd_putchar(variable);
					break;
				case '%':
					lcd_putchar('%');
					break;
				default:          // not implemented
					lcd_putchar('!');
			}
		}else	lcd_putchar(k); // found end of string
	}
	return;  
}

void lcd_init( void ) // must be run once before using the display
{
  delay(40);  // give LCD time to settle
  RS = 0;     // LCD in command-mode
  lcd_putchar(0b0011.0011); /* LCD starts in 8 bit mode          */
  lcd_putchar(0b0011.0010); /* change to 4 bit mode              */
  lcd_putchar(0b00101000);  /* two line (8+8 chars in the row)   */ 
  lcd_putchar(0b00001100);  /* display on, cursor off, blink off */
  lcd_putchar(0b00000001);  /* display clear                     */
  lcd_putchar(0b00000110);  /* increment mode, shift off         */
  RS = 1;    // LCD in character-mode
             // initialization is done!
}


/* 
  Borrowed predone delay funtion.
*/

void delay(char millisec)
/* 
  Delays a multiple of 1 milliseconds at 4 MHz (16F690 internal clock)
  using the TMR0 timer 
*/
{
    OPTION = 2;  /* prescaler divide by 8        */
    do  {
        TMR0 = 0;
        while ( TMR0 < 125)   /* 125 * 8 = 1000  */
            ;
    } while ( -- millisec > 0);
}

/* *********************************** */
/*            HARDWARE                 */
/* *********************************** */

/*
         ___________  ___________
        |           \/           |
  +5V---|Vdd     16F690       Vss|---GND
        |RA5        RA0/AN0/(PGD)|
        |RA4            RA1/(PGC)|
        |RA3/!MCLR/(Vpp)  RA2/INT|->- Potentiometer
        |RC5/CCP              RC0|->-D4
        |RC4                  RC1|->-D5
  D7 -<-|RC3                  RC2|->-D6
        |RC6                  RB4|->- RS
        |RC7               RB5/Rx|
Butt -<-|RB7/Tx               RB6|->- EN
        |________________________| 

*/

/*
           LCD two lines, Line length 16 characters
           Internal ic: HD44780A00		   
           _______________
          |               |
          |         Vss  1|--- GND  
          |         Vdd  2|--- +5V
          |    Contrast  3|-<- Pot
          |          RS  4|-<- RB4
          |      RD/!WR  5|--- 0, GND
          |          EN  6|-<- RB6
          |          D0  7|
          |          D1  8|
          |          D2  9|
          |          D3 10|
          |          D4 11|-<- RC0
          |          D5 12|-<- RC1 
          |          D6 13|-<- RC2
          |          D7 14|-<- RC3 
          |_______________|						  
*/
